# Fritzing sketch boot (saved by Fritzing 0.9.4)

parts:
  Bauteil1 = u-blox NEO-6M GPS Breakout
  U2 = MPU 9250 Breakout [package="SIP (Single Inline) [THT]"]
  U3 = LM2596 step down module
  BAT2 = Battery Holders [package=lipo-1100mAh]
  U4 = SWITCH_SPDT [package=kps-1290]
  U1 = ESP32S-HiLetgo [part_number=ESP32S-HiLetgo]
  L298N1 = L298N DC motor driver
  M1 = DC Motor
  M2 = DC Motor
  J1 = Camdenboss CTB0158-2 [part_number=CTB0158-2 package=THT]
  Bauteil3 = XBee Explorer Regulated
  Q1 = MOSFET-NCHANNEL [package=to220v]
  R1 = Resistor [tolerance=±20% resistance=100k package=THT]
  C1 = Electrolytic Capacitor [capacitance=47µF package="100 mil [THT, electrolytic]"]
  IC1 = 24LC256 [package=THT]

nets:
  GND: Bauteil1.GND, U2.GND, U3.IN-, U3.OUT-, BAT2.-, U1.GND, L298N1.GND, Bauteil3.GND, Q1.S, R1.Pin_0, C1.-, IC1.A0, IC1.A1, IC1.A2, IC1.0V, IC1.WP_-_Write_Protect
  VCC: Bauteil1.VCC, U3.OUT+, U1.GPIO11, U1.VIN, J1.pin1, Bauteil3.5V
  N1: Bauteil1.TXD, U1.GPIO13
  N2: U2.VCC, U1.3.3, IC1.+V
  N3: U2.SCL, U1.GPIO22, IC1.SCL_-_I2C_Clock
  N4: U2.SDA, U1.GPIO21, IC1.SDA_-_I2C_Data
  N5: U3.IN+, U4.P, L298N1.12V, C1.+
  N6: BAT2.+, U4.O
  N7: U1.GPIO25, Q1.G, R1.Pin_1
  N8: U1.GPIO14, Bauteil3.DIN
  N9: U1.GPIO12, Bauteil3.DOUT
  N10: L298N1.OUT1, M2.pin_1
  N11: L298N1.OUT2, M2.pin_2
  N12: L298N1.OUT3, M1.pin_2
  N13: L298N1.OUT4, M1.pin_1
  N14: J1.pin2, Q1.D

custom parts:
  MPU 9250 Breakout: Generic MPU 9250 Breakout Board
  LM2596 step down module: LM2596 DC-DC step down power supply module 3 A.
  ESP32S-HiLetgo: HiLetgo ESP-WROOM-32 ESP32 ESP-32S Development Board 2.4GHz Dual-Mode WiFi + Bluetooth Dual Cores Microcontroller The ESP32 integrated with Antenna switches, RF Balun, power amplifiers, low-noise amplifiers, filters, and management modules, and the entire solution occupies the least area of PCB. 2.4 GHz Wi-Fi plus Bluetooth dual-mode chip, with TSMC Ultra-low power consumption 40nm technology,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
  L298N DC motor driver: 2x DC motor driver with 78M05 positive voltage regulator (7..35 V) L298N: max 46 V, 2 A Set 5 V Enable jumper to enable 5 V regultor (needed for the L298N) and +5 V output at screw terminal or supply external +5 V at screw terminal Set ENA and/or ENB to +5 V to enable motor permanently or supply ENA and/or ENB with PWM signal IN1 and IN2 set rotation directory for motor A (OUT1/OUT2) IN2 and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
